// Logisim project control-logic.circ as structural Verilog: 1 circuit, main circuit control_logic
module control_logic (
  input  [31:0] Instruction,
  input  BrEq,
  input  BrLt,
  output PCSel,
  output RegWEn,
  output [2:0] ImmSel,
  output BrUn,
  output ASel,
  output BSel,
  output [3:0] ALUSel,
  output MemWEn,
  output [1:0] WBSel
);

  wire and_1_out, and_2_out, and_3_out, and_4_out, and_5_out, demultiplexer_1_out0, demultiplexer_1_out1,
       demultiplexer_1_out2, demultiplexer_1_out3, not_1_out, not_2_out, not_3_out, not_4_out, not_5_out,
       not_6_out, not_7_out, not_8_out, or_1_out, or_2_out, or_3_out, Plus1_out, Plus2_out, Plus4_out;
  wire [1:0] priority_encoder_1_out, priority_encoder_2_out;
  wire [2:0] priority_encoder_3_out;
  wire [5:0] adder_1_out, adder_2_out, adder_3_out, FinalPos, multiplexer_1_out, multiplexer_3_out, ROMInput,
       subtractor_1_out;
  wire [15:14] rom_1_data;

  Demultiplexer #(.enable("false"), .select(3)) demultiplexer_1 (
    .out0(demultiplexer_1_out0), .out1(demultiplexer_1_out1), .out2(demultiplexer_1_out2),
    .out3(demultiplexer_1_out3), .in(1'b1), .sel(Instruction[6:4]));  // open: out4, out5, out6, out7
  not not_1 (not_1_out, Instruction[14]);
  not not_2 (not_2_out, Instruction[13]);
  not not_3 (not_3_out, Instruction[30]);
  ROM #(.addrWidth(6), .dataWidth(16)) rom_1 (
    .addr(ROMInput), .data({rom_1_data, WBSel, MemWEn, ALUSel, BSel, ASel, BrUn, ImmSel, RegWEn}));
  and and_1 (and_1_out, not_1_out, not_2_out, Instruction[25]);
  not not_4 (not_4_out, Instruction[13]);
  not not_5 (not_5_out, Instruction[12]);
  not not_6 (not_6_out, Instruction[14]);
  or or_1 (or_1_out, demultiplexer_1_out3, demultiplexer_1_out3);
  not not_7 (not_7_out, Instruction[13]);
  not not_8 (not_8_out, Instruction[13]);
  and and_2 (and_2_out, Instruction[13], not_5_out);
  or or_2 (or_2_out, Instruction[12], Instruction[30]);
  and Plus1 (Plus1_out, demultiplexer_1_out3, and_1_out);
  and and_3 (and_3_out, demultiplexer_1_out3, Instruction[14], not_8_out, not_3_out);
  and and_4 (and_4_out, demultiplexer_1_out1, not_3_out, Instruction[14], not_4_out);
  Adder #(.width(6)) adder_1 (.a({3'b000, Instruction[14:12]}), .b(6'b000010), .out(adder_1_out));  // open: cin, cout
  or or_3 (or_3_out, Instruction[14], and_2_out);
  and and_5 (and_5_out, not_6_out, or_2_out);
  and Minus1 (Plus1_out, or_1_out, Instruction[14], not_7_out);
  // OR_Gate Minus1Test has open pins: in0=and_3_out, in1=and_4_out, out=open
  Adder #(.width(6)) adder_2 (.a(adder_1_out), .b(6'b000010), .out(adder_2_out));  // open: cin, cout
  and Plus4 (Plus4_out, demultiplexer_1_out3, or_3_out);
  and Plus2 (Plus2_out, demultiplexer_1_out3, and_5_out);
  Subtractor #(.width(6)) subtractor_1 (
    .a(multiplexer_1_out), .b(6'b000001), .out(subtractor_1_out));  // open: bin, bout
  Priority_Encoder #(.select(2)) priority_encoder_1 (
    .in0(1'b1), .in1(Plus4_out), .in2(Plus2_out), .out(priority_encoder_1_out));  // open: in3, gs, en_out, en_in
  Adder #(.width(6)) adder_3 (.a(subtractor_1_out), .b(6'b000010), .out(adder_3_out));  // open: cin, cout
  Multiplexer #(.enable("false"), .select(2), .width(6)) multiplexer_1 (
    .in0({3'b000, Instruction[14:12]}), .in1(adder_2_out), .in2(adder_1_out), .out(multiplexer_1_out),
    .sel(priority_encoder_1_out));  // open: in3
  Priority_Encoder #(.select(2)) priority_encoder_2 (
    .in0(1'b1), .in1(Plus1_out), .in2(Plus1_out), .out(priority_encoder_2_out));  // open: in3, gs, en_out, en_in
  Multiplexer #(.enable("false"), .select(2), .width(6)) multiplexer_2 (
    .in0(multiplexer_1_out), .in1(adder_3_out), .in2(subtractor_1_out), .out(FinalPos),
    .sel(priority_encoder_2_out));  // open: in3
  Multiplexer #(.enable("false"), .select(3), .width(6)) multiplexer_3 (
    .in0({6{1'b0}}), .in2(6'b001111), .out(multiplexer_3_out), .sel(priority_encoder_3_out));  // open: in1, in3, in4, in5, in6, in7
  Priority_Encoder priority_encoder_3 (
    .in0(demultiplexer_1_out3), .in2(demultiplexer_1_out1), .out(priority_encoder_3_out));  // open: in1, in3, in4, in5, in6, in7, en_in, gs, en_out
  Adder #(.width(6)) adder_4 (.a(multiplexer_3_out), .b(FinalPos), .out(ROMInput));  // open: cin, cout

  // Other names for the same wires on the sheet: Opcode[6:0] = Instruction[6:0]; Funct77thDig = Instruction[25];
  //   Funct72ndDig = Instruction[30]; Funct3[2:0] = Instruction[14:12]; Position[2:0] = Instruction[14:12]

  // Notes on the sheet:
  //   INPUTS to your circuit
  //   Connect ROM Input here ->
  //   contents of rom_1 (hex, n*v repeats v):
  //   1001 1401 1601 1081 1481 1581 1101 1201 1281 1681 1301 1381 0 0 0 1043 10c3 1143 1243 12c3 16c3 1343
  //   13c3
  //   ROM FOR CONTROL LOGIC
  //   DON'T CHANGE THE LOCATIONS OF THE INPUTS AND OUTPUTS!
  //   This is only if you choose to do the ROM option
  //   CONNECT
  //   WIRE
  //   TO
  //   USE
  //   ROM
  //   OUTPUT from your circuit
  //   Reminder: If using ROM, use combinational logic for PCSel
endmodule
